// Logisim project Pr_2_2_3.circ as structural Verilog: 2 circuits, main circuit main
module main (
  input  in_1,
  input  in_2,
  output out_3
);

  wire clock_1_out, local_sfm_1_out, local_sfm_2_out, or_1_out;

  Clock clock_1 (.out(clock_1_out));
  local_sfm local_sfm_1 (.CLK(clock_1_out), .OUT(local_sfm_1_out), .IN1(in_1), .IN2(in_2));
  local_sfm local_sfm_2 (.CLK(clock_1_out), .OUT(local_sfm_2_out), .IN1(in_2), .IN2(in_1));
  or or_1 (or_1_out, local_sfm_1_out, local_sfm_2_out);
  T_Flip_Flop t_ff_1 (.clk(or_1_out), .T(clock_1_out), .Q(out_3));  // open: Qn, preset, reset, en
endmodule

module local_sfm (
  input  IN1,
  input  IN2,
  input  CLK,
  output OUT
);

  wire rom_2_data;
  wire [2:0] rom_1_data;
  wire [4:2] register_1_q;

  ROM #(.addrWidth(5), .dataWidth(3)) rom_1 (.addr({register_1_q, IN1, IN2}), .data(rom_1_data));  // open: sel
  Register #(.width(3)) register_1 (.D(rom_1_data), .Q(register_1_q), .clk(CLK));  // open: en, clr
  ROM #(.addrWidth(5), .dataWidth(1)) rom_2 (.addr({register_1_q, IN1, IN2}), .data(rom_2_data));  // open: sel
  D_Flip_Flop d_ff_1 (.clk(CLK), .D(rom_2_data), .Q(OUT));  // open: Qn, preset, en, reset

  // Notes on the sheet:
  //   contents of rom_1 (hex, n*v repeats v):
  //   0 1 2 0 0 1 2 3 0 1 2 4 0 1 2 3 0 1 2 4
  //   contents of rom_2 (hex, n*v repeats v):
  //   14*0 1 0 0 1
endmodule
