// Logisim project counter_on_jk_trigger_example.circ as structural Verilog: 1 circuit, main circuit main
module main (
  output out_1,
  output out_2,
  output out_3,
  output out_4
);

  wire clock_1_out, nor_1_out, nor_2_out, nor_3_out, nor_4_out, nor_5_out, nor_6_out, nor_7_out;

  nor nor_1 (nor_1_out, ~out_2, ~out_3);  // NOR_Gate
  nor nor_2 (nor_2_out, out_3, out_4);
  nor nor_3 (nor_3_out, out_1, ~out_3);  // NOR_Gate
  nor nor_4 (nor_4_out, ~out_1, ~out_4);  // NOR_Gate
  nor nor_5 (nor_5_out, ~out_1, ~out_3);  // NOR_Gate
  Clock clock_1 (.out(clock_1_out));
  nor nor_6 (nor_6_out, nor_2_out, nor_2_out);
  nor nor_7 (nor_7_out, nor_4_out, nor_4_out);
  Hex_Digit_Display hex_digit_display_1 (.value({out_1, out_2, out_3, out_4}));  // open: dp
  J_K_Flip_Flop j_k_ff_1 (.J(nor_1_out), .clk(clock_1_out), .K(nor_6_out), .Q(out_1));  // open: Qn, preset, en, reset
  J_K_Flip_Flop j_k_ff_2 (.J(nor_3_out), .clk(clock_1_out), .K(out_3), .Q(out_2));  // open: Qn, preset, en, reset
  J_K_Flip_Flop j_k_ff_3 (.J(nor_7_out), .clk(clock_1_out), .K(1'b1), .Q(out_3));  // open: Qn, preset, en, reset
  J_K_Flip_Flop j_k_ff_4 (.J(nor_5_out), .clk(clock_1_out), .K(out_1), .Q(out_4));  // open: Qn, preset, en, reset

  // Other names for the same wires on the sheet: Q0 = out_4; Q1 = out_3; Q2 = out_2; Q3 = out_1

  // Notes on the sheet:
  //   S3
  //   S2
  //   S1
  //   S0
endmodule
